# Fritzing sketch ESP-01 Temperature Sensor (saved by Fritzing 0.9.3b)
circuit board: 2.7525cm x 2.58723cm

parts:
  R1 = Resistor [tolerance=±5% resistance=4.7k package=THT]
  DS1 = DS18B20 1-Wire Temperature Sensor [part_number=DS18B20]
  X1 = USB Connectors [package=usb-b-pth]
  ESP01 = ESP8266 WiFi Module [part_number=ESP8266]
  U1 = V_REG_LD1117VXX [package=78xxl]

nets:
  N1: R1.Pin_0, DS1.DQ, ESP01.GPIO_0
  VDD: R1.Pin_1, DS1.VDD, ESP01.VCC, U1.OUT
  GND: DS1.GND, X1.GND, ESP01.GND, U1.GND
  N2: X1.VBUS, U1.IN

custom parts:
  ESP8266 WiFi Module: Generic WiFi Module based on the ESP8266 with onboard PCB antenna and UART communications
